// Logisim project FA_8.circ as structural Verilog: 2 circuits, main circuit FA_1bit
module FA_1bit (
  input  A,
  input  B,
  input  C,
  output S,
  output P
);

  wire and_1_out, and_2_out, and_3_out, and_4_out, and_5_out, and_6_out, and_7_out, not_1_out, not_2_out,
       not_3_out;

  not not_1 (not_1_out, A);
  not not_2 (not_2_out, B);
  not not_3 (not_3_out, C);
  and and_1 (and_1_out, not_1_out, not_2_out, C);
  and and_2 (and_2_out, not_1_out, B, not_3_out);
  and and_3 (and_3_out, A, not_2_out, not_3_out);
  and and_4 (and_4_out, A, B, C);
  and and_5 (and_5_out, B, C);
  and and_6 (and_6_out, A, C);
  or or_1 (P, and_5_out, and_6_out, and_7_out);
  and and_7 (and_7_out, A, B);
  or or_2 (S, and_1_out, and_2_out, and_3_out, and_4_out);
endmodule

module FA_8bit (
  input  in_1,
  input  in_2,
  input  in_3,
  input  in_4,
  input  in_5,
  input  in_6,
  input  in_7,
  input  in_8,
  input  in_9,
  input  in_10,
  input  in_11,
  input  in_12,
  input  in_13,
  input  in_14,
  input  in_15,
  input  in_16,
  input  in_17,
  output out_18,
  output out_19,
  output out_20,
  output out_21,
  output out_22,
  output out_23,
  output out_24,
  output out_25,
  output out_26
);

  wire F0_p, F1_p, F2_p, F3_p, F4_p, F5_p, F6_p;

  FA_1bit F0 (.A(in_9), .B(in_17), .C(in_1), .S(out_25), .P(F0_p));
  FA_1bit F1 (.A(in_8), .B(in_16), .C(F0_p), .S(out_24), .P(F1_p));
  FA_1bit F2 (.A(in_7), .B(in_15), .C(F1_p), .S(out_23), .P(F2_p));
  FA_1bit F3 (.A(in_6), .B(in_14), .C(F2_p), .S(out_22), .P(F3_p));
  FA_1bit F4 (.A(in_5), .B(in_13), .C(F3_p), .S(out_21), .P(F4_p));
  FA_1bit F5 (.A(in_4), .B(in_12), .C(F4_p), .S(out_20), .P(F5_p));
  FA_1bit F6 (.A(in_3), .B(in_11), .C(F5_p), .S(out_19), .P(F6_p));
  FA_1bit F7 (.A(in_2), .B(in_10), .C(F6_p), .S(out_18), .P(out_26));
endmodule
