// Logisim project automat.circ as structural Verilog: 1 circuit, main circuit Ttrigger
module Ttrigger (
  output out_1,
  output out_2,
  output out_3
);

  wire clock_1_out, nand_1_out, nand_2_out, or_1_out;

  Clock clock_1 (.out(clock_1_out));
  T_Flip_Flop Q0 (.T(1'b1), .clk(clock_1_out), .Q(out_3));  // open: Qn, reset, preset
  nand nand_1 (nand_1_out, out_3, out_3);
  T_Flip_Flop Q1 (.T(nand_1_out), .clk(clock_1_out), .Q(out_2));  // open: Qn, reset, preset
  or or_1 (or_1_out, out_3, out_2);
  nand nand_2 (nand_2_out, or_1_out, or_1_out);
  T_Flip_Flop t_ff_1 (.T(nand_2_out), .clk(clock_1_out), .Q(out_1));  // open: Qn, reset, preset
endmodule
