// Logisim project bcd2421.circ as structural Verilog: 4 circuits, main circuit main
module main (
  input  in_1,
  input  in_2,
  input  in_3,
  input  in_4,
  input  in_5,
  input  in_6,
  input  in_7,
  input  in_8,
  output out_9,
  output out_10,
  output out_11,
  output out_12,
  output out_13,
  output out_14,
  output out_15,
  output out_16
);

  wire encoder2421_1_x1, encoder2421_1_x2, encoder2421_1_x3, encoder2421_1_x4, encoder2421_2_x1,
       encoder2421_2_x2, encoder2421_2_x3, encoder2421_2_x4, fa1_bit_1_p, fa1_bit_1_s, fa1_bit_2_p,
       fa1_bit_2_s, fa1_bit_3_p, fa1_bit_3_s, fa1_bit_4_p, fa1_bit_4_s;

  Encoder2421 encoder2421_1 (
    .A(in_1), .B(in_2), .C(in_3), .D(in_4), .X1(encoder2421_1_x1), .X2(encoder2421_1_x2),
    .X3(encoder2421_1_x3), .X4(encoder2421_1_x4));
  Encoder2421 encoder2421_2 (
    .A(in_5), .B(in_6), .C(in_7), .D(in_8), .X1(encoder2421_2_x1), .X2(encoder2421_2_x2),
    .X3(encoder2421_2_x3), .X4(encoder2421_2_x4));
  FA1_bit fa1_bit_1 (.A(encoder2421_1_x4), .B(encoder2421_2_x4), .C(1'b0), .S(fa1_bit_1_s), .P(fa1_bit_1_p));
  FA1_bit fa1_bit_2 (.A(encoder2421_1_x3), .B(encoder2421_2_x3), .C(fa1_bit_1_p), .S(fa1_bit_2_s), .P(fa1_bit_2_p));
  FA1_bit fa1_bit_3 (.A(encoder2421_1_x2), .B(encoder2421_2_x2), .C(fa1_bit_2_p), .S(fa1_bit_3_s), .P(fa1_bit_3_p));
  FA1_bit fa1_bit_4 (.A(encoder2421_1_x1), .B(encoder2421_2_x1), .C(fa1_bit_3_p), .S(fa1_bit_4_s), .P(fa1_bit_4_p));
  Decoder2421 decoder2421_1 (
    .A(fa1_bit_4_p), .B(fa1_bit_4_s), .C(fa1_bit_3_s), .D(fa1_bit_2_s), .E(fa1_bit_1_s), .X1(out_9),
    .X2(out_10), .X3(out_11), .X4(out_12), .X5(out_16), .X6(out_15), .X7(out_14), .X8(out_13));
endmodule

module Encoder2421 (
  input  A,
  input  B,
  input  C,
  input  D,
  output X1,
  output X2,
  output X3,
  output X4
);

  wire and_1_out, and_2_out, and_3_out, and_4_out, not_1_out, not_2_out, not_3_out;

  not not_1 (not_1_out, A);
  not not_2 (not_2_out, B);
  not not_3 (not_3_out, C);
  or or_1 (X1, B, A);
  and and_1 (and_1_out, B, C);
  and and_2 (and_2_out, not_1_out, not_2_out);
  and and_3 (and_3_out, not_1_out, C);
  and and_4 (and_4_out, A, not_3_out);
  or or_2 (X2, and_1_out, and_2_out);
  or or_3 (X3, and_3_out, and_4_out);

  assign X4 = D;
endmodule

module Decoder2421 (
  input  A,
  input  B,
  input  C,
  input  D,
  input  E,
  output X1,
  output X2,
  output X3,
  output X4,
  output X5,
  output X6,
  output X7,
  output X8
);

  wire and_2_out, and_3_out, and_4_out, and_5_out, and_6_out, and_7_out, and_8_out, and_9_out, and_10_out,
       and_11_out, and_12_out, and_13_out, and_14_out, and_15_out, and_16_out, and_17_out, and_18_out,
       and_19_out, and_20_out, and_21_out, and_22_out, and_23_out, and_24_out, and_25_out, not_1_out,
       not_2_out, not_3_out, not_4_out, not_5_out;

  not not_1 (not_1_out, A);
  not not_2 (not_2_out, B);
  not not_3 (not_3_out, C);
  not not_4 (not_4_out, D);
  not not_5 (not_5_out, E);
  and and_1 (X3, A, B);
  and and_2 (and_2_out, A, not_2_out);
  and and_3 (and_3_out, not_1_out, B, C, D);
  and and_4 (and_4_out, not_1_out, B, not_3_out, D);
  and and_5 (and_5_out, not_1_out, B, C, not_4_out);
  and and_6 (and_6_out, A, not_2_out, D, E);
  and and_7 (and_7_out, A, not_2_out, C);
  and and_8 (and_8_out, A, C, D);
  and and_9 (and_9_out, not_1_out, B, not_4_out, E);
  and and_10 (and_10_out, A, C, E);
  and and_11 (and_11_out, not_1_out, B, not_3_out, D);
  and and_12 (and_12_out, not_1_out, B, C, not_4_out);
  and and_13 (and_13_out, A, not_2_out, D, not_5_out);
  and and_14 (and_14_out, A, not_2_out, C);
  and and_15 (and_15_out, A, C, D);
  and and_16 (and_16_out, not_1_out, B, not_3_out, not_5_out);
  and and_17 (and_17_out, A, C, not_5_out);
  and and_18 (and_18_out, not_1_out, not_2_out, D);
  and and_19 (and_19_out, not_1_out, B, not_4_out, E);
  and and_20 (and_20_out, not_1_out, B, C, not_4_out);
  and and_21 (and_21_out, A, not_2_out, not_3_out, not_4_out);
  and and_22 (and_22_out, not_2_out, C, D);
  and and_23 (and_23_out, A, B, not_3_out, D);
  and and_24 (and_24_out, B, C, not_4_out, E);
  and and_25 (and_25_out, not_2_out, D, E);
  or or_1 (X4, and_2_out, and_3_out);
  or or_2 (X5, and_4_out, and_5_out, and_6_out, and_7_out, and_8_out, and_9_out, and_10_out);
  or or_3 (X6, and_11_out, and_12_out, and_13_out, and_14_out, and_15_out, and_16_out, and_17_out);
  or or_4 (X7, and_18_out, and_19_out, and_20_out, and_21_out, and_22_out, and_23_out, and_24_out, and_25_out);

  assign X1 = 1'b0;
  assign X2 = 1'b0;
  assign X8 = E;
endmodule

module FA1_bit (
  input  A,
  input  B,
  input  C,
  output S,
  output P
);

  wire and_1_out, and_2_out, and_3_out, and_4_out, and_5_out, and_6_out, and_7_out, not_1_out, not_2_out,
       not_3_out;

  not not_1 (not_1_out, A);
  not not_2 (not_2_out, B);
  not not_3 (not_3_out, C);
  and and_1 (and_1_out, not_1_out, not_2_out, C);
  and and_2 (and_2_out, not_1_out, B, not_3_out);
  and and_3 (and_3_out, A, not_2_out, not_3_out);
  and and_4 (and_4_out, A, B, C);
  and and_5 (and_5_out, B, C);
  and and_6 (and_6_out, A, C);
  or or_1 (P, and_5_out, and_6_out, and_7_out);
  and and_7 (and_7_out, A, B);
  or or_2 (S, and_1_out, and_2_out, and_3_out, and_4_out);
endmodule
